# Fritzing sketch Interceptor (saved by Fritzing 0.9.3b)
perfboards: 2

parts:
  DS1 = DS1809 [part_number=DS1809 package=DS1806]
  Part1 = Arduino Uno (Rev3)  # not connected
  J1 = female pin header, 7 pins [form="♀ (female)"]
  J3 = female pin header, 3 pins [form="♀ (female)"]
  J4 = female pin header, 3 pins [form="♀ (female)"]
  J5 = female pin header, 3 pins [form="♀ (female)"]
  J6 = female pin header, 3 pins [form="♀ (female)"]
  J2 = female pin header, 11 pins [form="♀ (female)"]
  DS2 = DS1809 [part_number=DS1809 package=DS1806]  # not connected
  J7 = female pin header, 7 pins [form="♀ (female)"]  # not connected
  J8 = female pin header, 3 pins [form="♀ (female)"]  # not connected
  J9 = female pin header, 3 pins [form="♀ (female)"]  # not connected
  J10 = female pin header, 3 pins [form="♀ (female)"]  # not connected
  J11 = female pin header, 3 pins [form="♀ (female)"]  # not connected
  J12 = female pin header, 11 pins [form="♀ (female)"]  # not connected

nets:
  N1: DS1.RH, J6.pin1
  N2: DS1.UC, J1.pin7, J3.pin1, J4.pin1, J5.pin3, J6.pin3, J2.pin1
  N3: DS1.STR, J5.pin1
  N4: DS1.RL, J2.pin5
  N5: DS1.GND, J1.pin3, J2.pin8
  N6: DS1.RW, J1.pin5, J2.pin6
  N7: DS1.DC, J2.pin9
  N8: DS1.VCC, J1.pin6, J3.pin2, J4.pin2, J5.pin2, J6.pin2, J2.pin2
  N9: J1.pin1, J2.pin11
  N10: J1.pin2, J2.pin10
  N11: J1.pin4, J2.pin7
  N12: J3.pin3, J2.pin3
  N13: J4.pin3, J2.pin4

notes:
  GND
  5V
  A0
  A1
  LDAC 8
  SO 12
  CLK 13
  SI 11
  CS 10
  CS 9
  INT 2
  Arduino
  CLK
  SO
  SI
  PEDAL B
  PEDAL A
  CAR A
  CAR B
  Can Bus Module
  D-to-A MCP4822
  Top of Board
  Bottom of Board - with Solder Traces
